# Fritzing sketch CTPowerMonitor (saved by Fritzing 0.9.9b)
circuit board: 3.3267cm x 2.53804cm
breadboards: 1

parts:
  C1 = Tantalum Capacitor [capacitance=10µF voltage=35V package="100 mil [THT, tantalum]"]
  Burden = Resistor [tolerance=±5% power=0.25 resistance=33 package=THT]
  R1 = Resistor [tolerance=±5% power=0.25 resistance=10k package=THT]
  R2 = Resistor [tolerance=±5% power=0.25 resistance=10k package=THT]
  CT1 = Audio Jack (TRS) 3.5mm [package="4Ucon 08780 [THT]"]
  J1 = male pin header, 3 pins [form="♂ (male)"]

nets:
  GND: C1.-, R2.Pin_0, J1.pin1
  N1: C1.+, Burden.Pin_1, R1.Pin_1, R2.Pin_1, CT1.Tip
  N2: Burden.Pin_0, CT1.Sleeve, J1.pin2
  3.3V: R1.Pin_0, J1.pin3

notes:
  10k
  10uF
  VCC
  A0
  GND
  ©2023 Adam Howell
