# Fritzing sketch ESP32QuadCT (saved by Fritzing 0.9.10b)
circuit board: 8.12548cm x 8.75631cm
breadboards: 1

parts:
  C1 = Tantalum Capacitor [capacitance=10µF voltage=35V package="100 mil [THT, tantalum]"]
  Burden1 = Resistor [tolerance=±5% power=0.25 resistance=33 package=THT]
  R1 = Resistor [tolerance=±5% power=0.25 resistance=10k package=THT]
  R2 = Resistor [tolerance=±5% power=0.25 resistance=10k package=THT]
  CT1 = Audio Jack (TRS) 3.5mm [package="4Ucon 08780 [THT]"]
  CT2 = Audio Jack (TRS) 3.5mm [package="4Ucon 08780 [THT]"]
  Burden2 = Resistor [tolerance=±5% power=0.25 resistance=33 package=THT]
  R3 = Resistor [tolerance=±5% power=0.25 resistance=10k package=THT]
  R4 = Resistor [tolerance=±5% power=0.25 resistance=10k package=THT]
  C2 = Tantalum Capacitor [capacitance=10µF voltage=35V package="100 mil [THT, tantalum]"]
  CT3 = Audio Jack (TRS) 3.5mm [package="4Ucon 08780 [THT]"]
  Burden3 = Resistor [tolerance=±5% power=0.25 resistance=33 package=THT]
  C3 = Tantalum Capacitor [capacitance=10µF voltage=35V package="100 mil [THT, tantalum]"]
  R5 = Resistor [tolerance=±5% power=0.25 resistance=10k package=THT]
  R6 = Resistor [tolerance=±5% power=0.25 resistance=10k package=THT]
  CT4 = Audio Jack (TRS) 3.5mm [package="4Ucon 08780 [THT]"]
  R8 = Resistor [tolerance=±5% power=0.25 resistance=10k package=THT]
  R7 = Resistor [tolerance=±5% power=0.25 resistance=10k package=THT]
  C5 = Tantalum Capacitor [capacitance=10µF voltage=35V package="100 mil [THT, tantalum]"]
  Burden4 = Resistor [tolerance=±5% power=0.25 resistance=33 package=THT]
  J1 = female pin header, 15 pins [form="♀ (female)"]
  J3 = female pin header, 15 pins [form="♀ (female)"]
  J4 = female pin header, 15 pins [form="♀ (female)"]
  J5 = female pin header, 15 pins [form="♀ (female)"]

nets:
  GND: C1.-, R2.Pin_0, R4.Pin_0, C2.-, C3.-, R6.Pin_0, R8.Pin_0, C5.-, J1.pin14, J4.pin14
  N1: C1.+, Burden1.Pin_1, R1.Pin_1, R2.Pin_1, CT1.Tip
  N2: Burden1.Pin_0, CT1.Sleeve, J1.pin2, J4.pin2
  5V: R1.Pin_0, R3.Pin_0, R5.Pin_0, R7.Pin_0, J3.pin15, J5.pin15
  N3: CT2.Sleeve, Burden2.Pin_0, J1.pin3, J4.pin3
  N4: CT2.Tip, Burden2.Pin_1, R3.Pin_1, R4.Pin_1, C2.+
  N5: CT3.Sleeve, Burden3.Pin_0, J1.pin4, J4.pin4
  N6: CT3.Tip, Burden3.Pin_1, C3.+, R5.Pin_1, R6.Pin_1
  N7: CT4.Sleeve, Burden4.Pin_0, J1.pin5, J4.pin5
  N8: CT4.Tip, R8.Pin_1, R7.Pin_1, C5.+, Burden4.Pin_1
  N9: J1.pin1, J4.pin1
  N10: J1.pin6, J4.pin6
  N11: J1.pin7, J4.pin7
  N12: J1.pin8, J4.pin8
  N13: J1.pin9, J4.pin9
  N14: J1.pin10, J4.pin10
  N15: J1.pin11, J4.pin11
  N16: J1.pin12, J4.pin12
  N17: J1.pin13, J4.pin13
  N18: J1.pin15, J4.pin15
  N19: J3.pin1, J5.pin1
  N20: J3.pin2, J5.pin2
  N21: J3.pin3, J5.pin3
  N22: J3.pin4, J5.pin4
  N23: J3.pin5, J5.pin5
  N24: J3.pin6, J5.pin6
  N25: J3.pin7, J5.pin7
  N26: J3.pin8, J5.pin8
  N27: J3.pin9, J5.pin9
  N28: J3.pin10, J5.pin10
  N29: J3.pin11, J5.pin11
  N30: J3.pin12, J5.pin12
  N31: J3.pin13, J5.pin13
  N32: J3.pin14, J5.pin14

notes:
  10k
  10uF
  VIN
  36
  GND
  ©2023 Adam Howell
  39
  34
  35
  3V3
  ESP32
  EN
  32
  33
  25
  26
  27
  14
  12
  13
  23 - MOSI
  30 Pin
  22 - SCL
  01 - TX0
  03 - RX0
  21 - SDA
  19 - MISO
  18 - SCK
  05 - SS
  17
  16
  04
  02
  15
  ADC1.3
  ADC1.6
  ADC1.7
  ADC1.4
  ADC1.5
  ADC1.0
