# Fritzing sketch QuadCTPowerMonitor (saved by Fritzing 0.9.9b)
circuit board: 4.41138cm x 8.698cm
breadboards: 1

parts:
  C1 = Tantalum Capacitor [capacitance=10µF voltage=35V package="100 mil [THT, tantalum]"]
  Burden1 = Resistor [tolerance=±5% power=0.25 resistance=33 package=THT]
  R1 = Resistor [tolerance=±5% power=0.25 resistance=10k package=THT]
  R2 = Resistor [tolerance=±5% power=0.25 resistance=10k package=THT]
  CT1 = Audio Jack (TRS) 3.5mm [package="4Ucon 08780 [THT]"]
  CT2 = Audio Jack (TRS) 3.5mm [package="4Ucon 08780 [THT]"]
  Burden2 = Resistor [tolerance=±5% power=0.25 resistance=33 package=THT]
  R3 = Resistor [tolerance=±5% power=0.25 resistance=10k package=THT]
  R4 = Resistor [tolerance=±5% power=0.25 resistance=10k package=THT]
  C2 = Tantalum Capacitor [capacitance=10µF voltage=35V package="100 mil [THT, tantalum]"]
  CT3 = Audio Jack (TRS) 3.5mm [package="4Ucon 08780 [THT]"]
  Burden3 = Resistor [tolerance=±5% power=0.25 resistance=33 package=THT]
  C3 = Tantalum Capacitor [capacitance=10µF voltage=35V package="100 mil [THT, tantalum]"]
  R5 = Resistor [tolerance=±5% power=0.25 resistance=10k package=THT]
  R6 = Resistor [tolerance=±5% power=0.25 resistance=10k package=THT]
  CT4 = Audio Jack (TRS) 3.5mm [package="4Ucon 08780 [THT]"]
  R8 = Resistor [tolerance=±5% power=0.25 resistance=10k package=THT]
  R7 = Resistor [tolerance=±5% power=0.25 resistance=10k package=THT]
  C5 = Tantalum Capacitor [capacitance=10µF voltage=35V package="100 mil [THT, tantalum]"]
  Burden4 = Resistor [tolerance=±5% power=0.25 resistance=33 package=THT]
  J1 = male pin header, 6 pins [form="♂ (male)"]

nets:
  GND: C1.-, R2.Pin_1, R4.Pin_1, C2.-, C3.-, R6.Pin_1, R8.Pin_1, C5.-, J1.pin6
  N1: C1.+, Burden1.Pin_1, R1.Pin_1, R2.Pin_0, CT1.Tip
  N2: Burden1.Pin_0, CT1.Sleeve, J1.pin2
  5V: R1.Pin_0, R3.Pin_0, R5.Pin_0, R7.Pin_0, J1.pin1
  N3: CT2.Sleeve, Burden2.Pin_0, J1.pin3
  N4: CT2.Tip, Burden2.Pin_1, R3.Pin_1, R4.Pin_0, C2.+
  N5: CT3.Sleeve, Burden3.Pin_0, J1.pin4
  N6: CT3.Tip, Burden3.Pin_1, C3.+, R5.Pin_1, R6.Pin_0
  N7: CT4.Sleeve, Burden4.Pin_0, J1.pin5
  N8: CT4.Tip, R8.Pin_0, R7.Pin_1, C5.+, Burden4.Pin_1

notes:
  10k
  10uF
  VCC
  A1
  GND
  ©2023 AJH
  A2
  A3
  A4
